# Fritzing sketch quiz (saved by Fritzing 0.9.3b)
breadboards: 3

parts:
  Raspberry_Pi_1 = Raspberry Pi 3 [part_number=RPI-3-V1.2]
  U1 = 74HC04_HEX_INVERTER [package=dil14]
  IC5 = SN74LS08N [package="DIP (Dual Inline) [THT]"]
  IC6 = SN74LS08N [package="DIP (Dual Inline) [THT]"]
  IC7 = SN74LS08N [package="DIP (Dual Inline) [THT]"]
  IC8 = SN74LS08N [package="DIP (Dual Inline) [THT]"]
  CD4044BE1 = CD4044BE [part_number=CD4044BE package="DIP (Dual Inline) [THT]"]
  CD4044BE2 = CD4044BE [part_number=CD4044BE package="DIP (Dual Inline) [THT]"]
  S1 = Momentary Switch [package=ksa_sealed_tac_switch]
  S2 = Momentary Switch [package=ksa_sealed_tac_switch]
  S3 = Momentary Switch [package=ksa_sealed_tac_switch]
  S4 = Momentary Switch [package=ksa_sealed_tac_switch]
  S5 = Momentary Switch [package=ksa_sealed_tac_switch]
  S6 = Momentary Switch [package=ksa_sealed_tac_switch]
  S7 = Momentary Switch [package=ksa_sealed_tac_switch]

nets:
  VCC: Raspberry_Pi_1.3v3, U1.VCC, IC5.VCC, IC6.VCC, IC7.VCC, IC8.VCC, CD4044BE1.ENABLE, CD4044BE1.VCC, CD4044BE2.ENABLE, CD4044BE2.VCC, S1.4, S2.4, S3.4, S4.4, S5.4, S6.4, S7.4
  GND: Raspberry_Pi_1.GND, U1.GND, IC5.GND, IC6.GND, IC7.GND, IC8.GND, CD4044BE1.GND, CD4044BE2.GND
  N1: Raspberry_Pi_1.GPIO25, U1.4A, CD4044BE1.Q4
  N2: Raspberry_Pi_1.GPIO24, U1.1A, CD4044BE1.Q1
  N3: Raspberry_Pi_1.GPIO23, U1.3A, CD4044BE1.Q3
  N4: Raspberry_Pi_1.GPIO18, U1.2A, CD4044BE1.Q2
  N5: Raspberry_Pi_1.GPIO15, U1.5A, CD4044BE2.Q1
  N6: Raspberry_Pi_1.GPIO14, U1.6A, CD4044BE2.Q2
  N7: U1.1Y, IC6.1A
  N8: U1.2Y, IC6.1B
  N9: U1.3Y, IC6.2B
  N10: U1.4Y, IC5.1B
  N11: U1.5Y, IC5.2B
  N12: U1.6Y, IC5.3B
  N13: IC5.1A, IC6.2Y
  N14: IC5.1Y, IC5.2A
  N15: IC5.2Y, IC5.3A
  N16: IC5.3Y, IC7.1B, IC7.2B, IC7.3B, IC7.4B, IC8.1B, IC8.2B
  N17: IC6.1Y, IC6.2A
  N18: IC7.1A, S3.1
  N19: IC7.1Y, CD4044BE1.S3
  N20: IC7.2A, S4.1
  N21: IC7.2Y, CD4044BE1.S4
  N22: IC7.3Y, CD4044BE2.S2
  N23: IC7.3A, S6.1
  N24: IC7.4Y, CD4044BE2.S1
  N25: IC7.4A, S5.1
  N26: IC8.1A, S1.1
  N27: IC8.1Y, CD4044BE1.S1
  N28: IC8.2A, S2.1
  N29: IC8.2Y, CD4044BE1.S2

notes:
  Q1 |green |18/24
  Q2 |grey |12/18
  Q3 |white |16/23
  Q4 |orange|22/25
  Q5_1|brown |10/15
  Q6_2|cyan |8/14

custom parts:
  SN74LS08N: IC containing quadruple 2-input positive-AND gates.
  CD4044BE: A Dual 2 to 4 DEMX / Decoder
